# Fritzing sketch arduino-serial (saved by Fritzing 0.7.7b)
breadboards: 1

parts:
  Arduino1 = Arduino
  LED1 = LED - 5mm [color="Red (633nm)" package="5 mm [THT]"]
  R2 = Resistor [tolerance=±5% resistance=10k package=THT]
  LED2 = LED - 5mm [color="Red (633nm)" package="5 mm [THT]"]
  LED3 = LED - 5mm [color="Red (633nm)" package="5 mm [THT]"]
  LED4 = LED - 5mm [color="Red (633nm)" package="5 mm [THT]"]
  R3 = Resistor [tolerance=±5% resistance=10k package=THT]
  R4 = Resistor [tolerance=±5% resistance=10k package=THT]
  R5 = Resistor [tolerance=±5% resistance=10k package=THT]

nets:
  N1: Arduino1.GND, LED1.cathode, LED2.cathode, LED3.cathode, LED4.cathode
  N2: Arduino1.D13, R2.Pin_0
  N3: Arduino1.D12, R3.Pin_0
  N4: Arduino1.D11, R4.Pin_0
  N5: Arduino1.D10, R5.Pin_0
  N6: LED1.anode, R2.Pin_1
  N7: LED2.anode, R3.Pin_1
  N8: LED3.anode, R5.Pin_1
  N9: LED4.anode, R4.Pin_1
